# Fritzing sketch 6_finger_aug (saved by Fritzing 0.9.8b)
breadboards: 1

parts:
  Part1 = PocketBeagle
  LED1 = LED - 5mm [color="Red (633nm)" current=0.030 package="5 mm [THT]"]
  LED2 = LED - 5mm [color="Green (555nm)" current=0.030 package="5 mm [THT]"]
  7SEG4 = 7-Segment LED I2C Backpack (white)  # not connected
  R1 = Resistor [tolerance=±5% power=0.25 resistance=2.2k package=THT]
  R2 = Resistor [tolerance=±5% power=0.25 resistance=2.2k package=THT]
  SERVO1 = Tower Pro SG90 servo [part_number=101246]
  R3 = TRIMPOT [package=trimpot_pth_s3_lock]
  S1 = Pushbutton [package="[THT]"]
  R4 = Resistor [tolerance=±5% power=0.25 resistance=2.2k package=THT]

nets:
  N1: Part1.3.3V, R1.Pin_1, R2.Pin_1, R3.CW, R4.Pin_1
  GND: Part1.GND, Part1.AIN.VREFN, LED1.cathode, LED2.cathode, SERVO1.GND, R3.CCW, S1.Pin_1, S1.Pin_2
  N2: Part1.AIN0(1.8V), R3.WIPER
  N3: Part1.VOUT, SERVO1.+5V
  N4: Part1.PWM0A, SERVO1.Signal
  N5: Part1.PWM1A, S1.Pin_3, S1.Pin_4, R4.Pin_0
  N6: Part1.GPIO58, LED2.anode
  N7: Part1.GPIO57, LED1.anode

custom parts:
  7-Segment LED I2C Backpack (white): 4-digit, 7-segment LED Display with I2C Control
  Tower Pro SG90 servo: Original file by John De Cristofaro http://www.adafruit.com/products/1449 Adafruit Feedback Servo (Small) Edited by: e-radionica.com 28/9/2015
